// Logisim project estacionamento.circ as structural Verilog
module main (
  input  RESET,
  input  in_2,
  input  in_3,
  output ERRO
);

  wire clock_1_out, controle_1_b1p, controle_1_cl, display_1_a, display_1_c, display_1_d, display_1_e,
       display_1_f, display_1_g, display_1_out_6, j_k_ff_1_q, j_k_ff_2_q, j_k_ff_2_qn, j_k_ff_3_q,
       j_k_ff_4_q, j_k_ff_4_qn, j_k_ff_5_q, j_k_ff_6_q, j_k_ff_6_qn, j_k_ff_8_qn;

  Clock clock_1 (.out(clock_1_out));
  controle controle_1 (
    .CLK(clock_1_out), .ENTRA(in_2), .SAI(in_3), .cl(controle_1_cl), .erro(ERRO), .b1p(controle_1_b1p));  // open: b2p
  J_K_Flip_Flop j_k_ff_1 (.J(1'b1), .K(1'b1), .clk(controle_1_b1p), .Q(j_k_ff_1_q), .reset(RESET));  // open: Qn, preset
  J_K_Flip_Flop j_k_ff_2 (
    .J(1'b1), .K(1'b1), .clk(controle_1_cl), .Q(j_k_ff_2_q), .Qn(j_k_ff_2_qn), .reset(RESET));  // open: preset
  J_K_Flip_Flop j_k_ff_3 (.J(1'b1), .K(1'b1), .clk(j_k_ff_1_q), .Q(j_k_ff_3_q), .reset(RESET));  // open: Qn, preset
  J_K_Flip_Flop j_k_ff_4 (
    .J(1'b1), .K(1'b1), .clk(j_k_ff_2_q), .Q(j_k_ff_4_q), .Qn(j_k_ff_4_qn), .reset(RESET));  // open: preset
  J_K_Flip_Flop j_k_ff_5 (.J(1'b1), .K(1'b1), .clk(j_k_ff_3_q), .Q(j_k_ff_5_q), .reset(RESET));  // open: Qn, preset
  J_K_Flip_Flop j_k_ff_6 (
    .J(1'b1), .K(1'b1), .clk(j_k_ff_4_q), .Q(j_k_ff_6_q), .Qn(j_k_ff_6_qn), .reset(RESET));  // open: preset
  J_K_Flip_Flop j_k_ff_7 (.J(1'b1), .K(1'b1), .clk(j_k_ff_5_q), .reset(RESET));  // open: Q, Qn, preset
  J_K_Flip_Flop j_k_ff_8 (.J(1'b1), .K(1'b1), .clk(j_k_ff_6_q), .Qn(j_k_ff_8_qn), .reset(RESET));  // open: Q, preset
  _7_Segment_Display u_7_segment_display_1 (
    .g(display_1_g), .f(display_1_f), .a(display_1_a), .b(display_1_out_6), .e(display_1_e), .d(display_1_d),
    .c(display_1_c));  // open: dp
  display display_1 (
    .a(display_1_a), .out_6(display_1_out_6), .c(display_1_c), .d(display_1_d), .e(display_1_e),
    .f(display_1_f), .g(display_1_g));  // open: in_1, B, in_3, in_4
endmodule

module display (
  input  in_1,
  input  B,
  input  in_3,
  input  in_4,
  output a,
  output out_6,
  output c,
  output d,
  output e,
  output f,
  output g
);

  wire and_1_out, and_2_out, and_3_out, and_4_out, and_5_out, and_6_out, and_7_out, and_8_out, and_9_out,
       and_10_out, and_11_out, and_12_out, and_13_out, and_14_out, and_15_out, and_16_out, and_17_out,
       and_18_out, and_19_out, and_20_out, and_21_out, and_22_out, and_23_out, not_1_out, not_2_out,
       not_3_out, not_4_out;

  not not_1 (not_1_out, in_1);
  not not_2 (not_2_out, B);
  not not_3 (not_3_out, in_3);
  not not_4 (not_4_out, in_4);
  and and_1 (and_1_out, not_2_out, not_4_out);
  and and_2 (and_2_out, B, in_4);
  and and_3 (and_3_out, not_1_out, not_2_out);
  and and_4 (and_4_out, not_1_out, not_3_out, not_4_out);
  and and_5 (and_5_out, not_2_out, not_3_out);
  and and_6 (and_6_out, not_1_out, in_3, in_4);
  and and_7 (and_7_out, not_1_out, in_4);
  and and_8 (and_8_out, not_2_out, not_3_out);
  and and_9 (and_9_out, not_1_out, B);
  and and_10 (and_10_out, not_2_out, not_4_out);
  and and_11 (and_11_out, not_2_out, in_3);
  and and_12 (and_12_out, B, not_3_out, in_4);
  and and_13 (and_13_out, in_3, not_4_out);
  and and_14 (and_14_out, not_2_out, not_4_out);
  and and_15 (and_15_out, in_3, not_4_out);
  and and_16 (and_16_out, in_1, in_3);
  and and_17 (and_17_out, in_1, B);
  and and_18 (and_18_out, not_3_out, not_4_out);
  and and_19 (and_19_out, B, not_3_out);
  and and_20 (and_20_out, B, not_4_out);
  and and_21 (and_21_out, not_2_out, in_3);
  and and_22 (and_22_out, B, not_3_out);
  and and_23 (and_23_out, in_3, not_4_out);
  or or_1 (a, and_1_out, in_3, and_2_out, in_1);
  or or_2 (out_6, and_3_out, and_4_out, and_5_out, and_6_out);
  or or_3 (c, and_7_out, and_8_out, and_9_out);
  or or_4 (d, and_10_out, and_11_out, and_12_out, and_13_out, in_1);
  or or_5 (e, and_14_out, and_15_out, and_16_out, and_17_out);
  or or_6 (f, and_18_out, and_19_out, and_20_out, in_1);
  or or_7 (g, and_21_out, and_22_out, in_1, and_23_out);
endmodule

module controle (
  input  CLK,
  input  ENTRA,
  input  SAI,
  output cl,
  output erro,
  output b1p,
  output b2p
);

  wire and_1_out, and_2_out, not_1_out, not_2_out;

  not not_1 (not_1_out, ENTRA);
  not not_2 (not_2_out, SAI);
  and and_1 (and_1_out, CLK, not_1_out, SAI);
  and and_2 (and_2_out, CLK, ENTRA, not_2_out);
  and and_3 (erro, CLK, ENTRA, SAI);
  and and_4 (b1p, CLK, ENTRA, not_2_out);
  and and_5 (b2p, CLK, not_1_out, SAI);
  or or_1 (cl, and_1_out, and_2_out);
endmodule
