// Logisim project hex.circ as structural Verilog: 3 circuits, main circuit main
module main (
  input  RESET,
  input  ENABLE
);

  wire clock_1_out, controle_1_pulso, controle_1_rst, display_1_a, display_1_b, display_1_c, display_1_d,
       display_1_e, display_1_f, display_1_g, j_k_ff_1_q, j_k_ff_1_qn, j_k_ff_2_q, j_k_ff_2_qn, j_k_ff_3_qn;

  Clock clock_1 (.out(clock_1_out));
  J_K_Flip_Flop j_k_ff_1 (
    .J(1'b1), .K(1'b1), .clk(controle_1_pulso), .Q(j_k_ff_1_q), .Qn(j_k_ff_1_qn), .reset(controle_1_rst));  // open: preset
  controle controle_1 (
    .CLK(clock_1_out), .RESET(RESET), .ENABLE(ENABLE), .pulso(controle_1_pulso), .rst(controle_1_rst));  // open: ativado
  J_K_Flip_Flop j_k_ff_2 (
    .J(1'b1), .K(1'b1), .clk(j_k_ff_1_q), .Q(j_k_ff_2_q), .Qn(j_k_ff_2_qn), .reset(controle_1_rst));  // open: preset
  J_K_Flip_Flop j_k_ff_3 (
    .J(1'b1), .K(1'b1), .clk(j_k_ff_2_q), .Qn(j_k_ff_3_qn), .reset(controle_1_rst));  // open: Q, preset
  display display_1 (
    .in_1(j_k_ff_3_qn), .in_2(j_k_ff_2_qn), .in_3(j_k_ff_1_qn), .a(display_1_a), .b(display_1_b),
    .c(display_1_c), .d(display_1_d), .e(display_1_e), .f(display_1_f), .g(display_1_g));
  _7_Segment_Display u_7_segment_display_1 (
    .g(display_1_g), .f(display_1_f), .a(display_1_a), .b(display_1_b), .e(display_1_e), .d(display_1_d),
    .c(display_1_c));  // open: dp
endmodule

module controle (
  input  CLK,
  input  RESET,
  input  ENABLE,
  output pulso,
  output rst,
  output ativado
);

  wire not_1_out;

  not not_1 (not_1_out, RESET);
  and and_1 (pulso, CLK, not_1_out, ENABLE);

  assign ativado = ENABLE;
  assign rst = RESET;
endmodule

module display (
  input  in_1,
  input  in_2,
  input  in_3,
  output a,
  output b,
  output c,
  output d,
  output e,
  output f,
  output g
);

  wire and_1_out, and_2_out, and_3_out, and_4_out, and_5_out, and_6_out, and_7_out, and_8_out, and_9_out,
       and_10_out, and_11_out, and_12_out, and_13_out, not_1_out, not_2_out, not_3_out;

  not not_1 (not_1_out, in_1);
  not not_2 (not_2_out, in_2);
  not not_3 (not_3_out, in_3);
  and and_1 (and_1_out, not_1_out, not_2_out);
  or or_1 (b, and_1_out, not_3_out, and_2_out);
  and and_2 (and_2_out, in_1, in_2);
  and and_3 (and_3_out, not_1_out, not_2_out, in_3);
  and and_4 (and_4_out, in_2, not_3_out);
  or or_2 (c, and_3_out, and_4_out, and_5_out);
  and and_5 (and_5_out, in_1, not_3_out);
  and and_6 (and_6_out, not_2_out, not_3_out);
  and and_7 (and_7_out, in_2, in_3);
  or or_3 (d, and_6_out, and_7_out, and_8_out);
  and and_8 (and_8_out, in_1, not_3_out);
  and and_9 (and_9_out, not_1_out, not_2_out);
  or or_4 (e, and_9_out, in_3, and_10_out);
  and and_10 (and_10_out, in_1, in_2);
  and and_11 (and_11_out, not_1_out, in_3);
  and and_12 (and_12_out, not_2_out, in_3);
  or or_5 (f, and_11_out, and_12_out, and_13_out);
  and and_13 (and_13_out, in_1, in_2, not_3_out);
  or or_6 (g, not_2_out, in_1);

  assign a = 1'b1;
endmodule
